# Fritzing sketch Nhom11 (saved by Fritzing 0.9.4)

parts:
  U1 = ESP8266 NodeMCU LoLin module
  Part1 = LCD1602-I2C
  U3 = GAS_SENSOR [package=mq-3]
  J1 = Piezo Speaker  # not connected
  M1 = fc-51 [package=THT]
  M2 = fc-51 [package=THT]

nets:
  N1: U1.D1, M1.pin1
  N2: U1.D2, M2.pin1
  N3: U1.3V3, U3.A1
  GND: U1.GND, Part1.GND, U3.B1, M1.pin2, M2.pin2
  N4: U1.D5, U1.VU, Part1.VCC, Part1.SDA
  N5: U1.D6, Part1.SCL
  N6: U1.Vin, M1.pin3, M2.pin3
  N7: U1.A0, U3.H1

custom parts:
  ESP8266 NodeMCU LoLin module: ESP8266 based NodeMCU
  LCD1602-I2C: A standard character display, usually with 2x16 characters. Comes in many colors with LCM1602 IIC attached.
